# Fritzing sketch 回路図 (saved by Fritzing 0.9.3b)
circuit board: 4.37cm x 3.64cm
breadboards: 1

parts:
  U2 = mystery part, 3 pins [chip_label=SERVO]
  U3 = mystery part, 3 pins [chip_label=SERVO]
  U4 = mystery part, 3 pins [chip_label=SERVO]
  IC2 = IC, SIP package, 3 pins [chip_label=TA48033S]
  U1 = mystery part, 3 pins [chip_label=SERVO]
  R18 = Resistor [tolerance=±5% resistance=10k package=THT]
  R19 = Resistor [tolerance=±5% resistance=10k package=THT]
  S3 = Pushbutton [package=THT]
  S4 = Pushbutton [package=THT]
  U5 = mystery part, 3 pins [chip_label=SERVO]
  IC5 = IC, DIP package, 20 pins [chip_label=FXMA108]
  IC1 = IC, DIP package, 18 pins [chip_label=WROOM02]
  R21 = Resistor [tolerance=±5% resistance=10k package=THT]
  C2 = Ceramic Capacitor [capacitance=100nF package="200 mil [THT, multilayer]"]
  C1 = Electrolytic Capacitor [capacitance=47µF package="100 mil [THT, electrolytic]"]
  R20 = Resistor [tolerance=±5% resistance=1k package=THT]
  LED1 = LED - 5mm [color="Red (633nm)" package="5 mm [THT]"]

nets:
  N1: U2.pin1, IC5.pin4
  5V: U2.pin2, U3.pin2, U4.pin2, IC2.pin1, U1.pin2, U5.pin2, IC5.pin1, C2.1
  GND: U2.pin3, U3.pin3, U4.pin3, IC2.pin2, U1.pin3, S3.leg0, S4.leg0, U5.pin3, IC5.pin10, IC5.pin11, IC1.pin9, R21.Pin_0, C2.0, C1.-
  N2: U3.pin1, IC5.pin5
  N3: U4.pin1, IC5.pin6
  3.3V: IC2.pin3, R18.Pin_1, R19.Pin_1, IC5.pin20, IC1.pin1, IC1.pin2, IC1.pin7, IC1.pin8, IC1.pin15, C1.+, R20.Pin_0
  N4: U1.pin1, IC5.pin3
  N5: R18.Pin_0, S3.leg1, IC1.pin14
  N6: R19.Pin_0, S4.leg1, IC1.pin10
  N7: IC5.pin15, IC1.pin6, R21.Pin_1
  N8: IC5.pin16, IC1.pin5
  N9: IC5.pin17, IC1.pin4
  N10: IC5.pin18, IC1.pin3
  N11: IC1.pin18, LED1.cathode
  N12: R20.Pin_1, LED1.anode
